# Fritzing sketch mClon (saved by Fritzing 0.9.3b)
breadboards: 1

parts:
  U1 = 74HC04_HEX_INVERTER [package=dil14]
  IC1 = L293D [package=THT]  # not connected
  R1 = Resistor [tolerance=±5% resistance=220 package=THT]
  S1 = Pushbutton [package="[THT]"]
  M1 = DC Motor  # not connected
  Componente1 = Arduino Uno (Rev3)  # not connected
  Componente2 = NeoPixel Stick [part_number=1426]  # not connected
  HC-SR04_Sensor_1 = HC-SR04 Ultrasonic Distance Sensor  # not connected
  M2 = fc-51 [package=THT]  # not connected
  M3 = fc-51 [package=THT]  # not connected
  IR1 = TSOP312.., 314.. [package=THT]  # not connected
  J1 = Piezo Speaker  # not connected
  Componente3 = VERTER 5V USB Buck-Boost  # not connected
  M4 = DC Motor  # not connected
  Componente4 = Lithium Ion Polymer Battery 3.7v 2500mAh [part_number=328]  # not connected

nets:
  N1: U1.VCC, R1.Pin_1
  N2: R1.Pin_0, S1.Pin_3, S1.Pin_4
  N3: S1.Pin_1, S1.Pin_2

custom parts:
  NeoPixel Stick: Make your own little LED strip arrangement with this stick of NeoPixel LEDs. We crammed 8 of the tiny 5050 (5mm x 5mm) smart RGB LEDs onto a PCB with mounting holes and a chainable design. Use only one microcontroller pin to control as many as you can chain together! Each LED is addressable as the driver chip is inside the LED. Each one has ~18mA constant current drive so the color will be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
  VERTER 5V USB Buck-Boost: VERTER can take battery voltages from 3-12VDC and output a nice 5V DC, which makes it a perfect universal power supply for your portable project! Where Verter really shines is when you have a battery or power range that can fluctuate a lot, or you don't know what you'll end up using.
  Lithium Ion Polymer Battery 3.7v 2500mAh: Lithium ion polymer (also known as 'lipo' or 'lipoly') batteries are thin, light and powerful. The output ranges from 4.2V when completely charged to 3.7V. This battery has a capacity of 2500mAh for a total of about 10 Wh. The batteries come pre-attached with a genuine 2-pin JST-PH connector as shown and include the necessary protection circuitry.
